# Fritzing sketch MAX7219 4x7 Single Sided PCB (saved by Fritzing 0.7.12b)
breadboards: 1

parts:
  IC1 = IC, DIP package, 24 pins [chip_label=MAX2719]
  J1 = female pin header, 6 pins [form="♀ (female)"]
  J2 = female pin header, 6 pins [form="♀ (female)"]
  R1 = Resistor [tolerance=±5% resistance=220 package=THT]
  J3 = female pin header, 5 pins [form="♀ (female)"]
  C1 = Electrolytic Capacitor [capacitance=1µF package="100 mil [THT, electrolytic]"]
  C2 = Ceramic Capacitor [capacitance=100nF package="100 mil [THT, multilayer]"]

nets:
  N1: IC1.pin1, J3.pin1
  N2: IC1.pin2, J2.pin6
  N3: IC1.pin4, IC1.pin13, J3.pin2, J3.pin4, C1.-, C2.0
  N4: IC1.pin6, J1.pin4
  N5: IC1.pin7, J1.pin1
  N6: IC1.pin11, J1.pin5
  N7: IC1.pin12, J3.pin3
  N8: IC1.pin14, J1.pin2
  N9: IC1.pin15, J1.pin3
  N10: IC1.pin16, J1.pin6
  N11: IC1.pin17, J2.pin5
  N12: IC1.pin18, R1.Pin_1
  N13: IC1.pin19, R1.Pin_0, J3.pin5, C1.+, C2.1
  N14: IC1.pin20, J2.pin4
  N15: IC1.pin21, J2.pin1
  N16: IC1.pin22, J2.pin3
  N17: IC1.pin23, J2.pin2
