# Fritzing sketch MAX7219 Dual Sided PCB  (saved by Fritzing 0.7.12b)
breadboards: 3

parts:
  IC3 = IC, DIP package, 24 pins [chip_label=MAX2719]
  J7 = female pin header, 6 pins [form="♀ (female)"]
  J8 = female pin header, 6 pins [form="♀ (female)"]
  R7 = Resistor [tolerance=±5% resistance=220 package=THT]
  J9 = female pin header, 5 pins [form="♀ (female)"]
  C6 = Ceramic Capacitor [capacitance=100nF package="100 mil [THT, multilayer]"]
  C5 = Electrolytic Capacitor [capacitance=1µF package="100 mil [THT, electrolytic]"]

nets:
  N1: IC3.pin1, J9.pin1
  N2: IC3.pin2, J7.pin6
  N3: IC3.pin4, J9.pin4, C6.0, C5.-
  N4: IC3.pin6, J8.pin4
  N5: IC3.pin7, J8.pin1
  N6: IC3.pin11, J8.pin5
  N7: IC3.pin12, J9.pin3
  N8: IC3.pin13, J9.pin2
  N9: IC3.pin14, J8.pin2
  N10: IC3.pin15, J8.pin3
  N11: IC3.pin16, J8.pin6
  N12: IC3.pin17, J7.pin5
  N13: IC3.pin18, R7.Pin_1
  N14: IC3.pin19, R7.Pin_0, J9.pin5, C6.1, C5.+
  N15: IC3.pin20, J7.pin4
  N16: IC3.pin21, J7.pin1
  N17: IC3.pin22, J7.pin3
  N18: IC3.pin23, J7.pin2
